# Fritzing sketch Schema_Progetto (saved by Fritzing 0.8.7b)
breadboards: 1

parts:
  U2 = 74HC595 [package="DIP16 [THT]"]
  U3 = 7-SEGMENT-DISPLAY-1_-RED [package=7-segment-1_pth]  # not connected
  Arduino_UNO = Arduino Uno (Rev3)

nets:
  GND: U2.GND, U2.OE, Arduino_UNO.GND
  VCC: U2.MR, U2.VCC, Arduino_UNO.5V
  N1: U2.SH_CP, Arduino_UNO.D6_PWM
  N2: U2.ST_CP, Arduino_UNO.D5_PWM
  N3: U2.DS, Arduino_UNO.D4
